// Logisim project lab1.circ as structural Verilog
module One_bit_comparator (
  input  A,
  input  B,
  output A___B,
  output A___B_2,
  output A___B_3
);

  wire and_2_out, and_3_out, not_1_out, not_2_out;

  not not_1 (not_1_out, A);
  not not_2 (not_2_out, B);
  and and_1 (A___B, not_2_out, A);
  and and_2 (and_2_out, A, B);
  and and_3 (and_3_out, not_2_out, not_1_out);
  and and_4 (A___B_3, not_1_out, B);
  or or_1 (A___B_2, and_2_out, and_3_out);

  // Notes on the sheet:
  //   A'
  //   B'
  //   AB'
  //   A'B
  //   AB+A'B'
endmodule
