// Logisim project lab2circuit.circ as structural Verilog
module BCD2_7SEG_DECO (
  input  w,
  input  x,
  input  y,
  input  z,
  output a,
  output b,
  output c,
  output d,
  output e,
  output f,
  output g
);

  wire and_1_out, and_2_out, and_3_out, and_4_out, and_5_out, and_6_out, and_7_out, and_8_out, and_9_out,
       and_10_out, and_11_out, and_12_out, and_13_out, and_14_out, and_15_out, and_16_out, not_1_out,
       not_2_out, not_3_out, not_4_out;

  not not_1 (not_1_out, w);
  not not_2 (not_2_out, x);
  not not_3 (not_3_out, y);
  not not_4 (not_4_out, z);
  and and_1 (and_1_out, z, x);
  and and_2 (and_2_out, not_4_out, not_2_out);
  and and_3 (and_3_out, not_3_out, not_4_out);
  and and_4 (and_4_out, z, y);
  and and_5 (and_5_out, not_4_out, not_2_out);
  and and_6 (and_6_out, not_2_out, y);
  and and_7 (and_7_out, y, not_4_out);
  and and_8 (and_8_out, z, not_3_out, x);
  and and_9 (and_9_out, not_4_out, not_2_out);
  and and_10 (and_10_out, not_4_out, y);
  and and_11 (and_11_out, not_4_out, not_3_out);
  and and_12 (and_12_out, not_3_out, x);
  and and_13 (and_13_out, x, not_4_out);
  and and_14 (and_14_out, not_2_out, y);
  and and_15 (and_15_out, y, not_4_out);
  and and_16 (and_16_out, x, not_3_out);
  or or_1 (a, y, w, and_1_out, and_2_out);
  or or_2 (b, not_2_out, and_3_out, and_4_out);
  or or_3 (c, not_3_out, z, x);
  or or_4 (d, w, and_5_out, and_6_out, and_7_out, and_8_out);
  or or_5 (e, and_9_out, and_10_out);
  or or_6 (f, w, and_11_out, and_12_out, and_13_out);
  or or_7 (g, w, and_14_out, and_15_out, and_16_out);
endmodule

module Test_BCD2 (
  input  [3:0] in_1
);

  wire bcd2_7seg_deco_1_a, bcd2_7seg_deco_1_b, bcd2_7seg_deco_1_c, bcd2_7seg_deco_1_d, bcd2_7seg_deco_1_e,
       bcd2_7seg_deco_1_f, bcd2_7seg_deco_1_g;

  BCD2_7SEG_DECO bcd2_7seg_deco_1 (
    .w(in_1[3]), .x(in_1[2]), .y(in_1[1]), .z(in_1[0]), .a(bcd2_7seg_deco_1_a), .b(bcd2_7seg_deco_1_b),
    .c(bcd2_7seg_deco_1_c), .d(bcd2_7seg_deco_1_d), .e(bcd2_7seg_deco_1_e), .f(bcd2_7seg_deco_1_f),
    .g(bcd2_7seg_deco_1_g));
  _7_Segment_Display u_7_segment_display_1 (
    .g(bcd2_7seg_deco_1_g), .f(bcd2_7seg_deco_1_f), .a(bcd2_7seg_deco_1_a), .b(bcd2_7seg_deco_1_b),
    .e(bcd2_7seg_deco_1_e), .d(bcd2_7seg_deco_1_d), .c(bcd2_7seg_deco_1_c));  // open: dp
endmodule
