// Logisim project lab4 .circ as structural Verilog: 13 circuits, main circuit main
module main (
  input  A,
  input  B,
  input  C,
  output [1:0] out_4
);

  wire and_1_out, and_2_out, BNEG;

  and and_1 (and_1_out, A, C);
  not not_1 (BNEG, B);
  and and_2 (and_2_out, A, BNEG);
  or or_1 (out_4[0], and_2_out, and_1_out);
  // AND_Gate and_3 is placed but not wired

  assign out_4[1] = B;
endmodule

module ALU_1bit (
  input  Cin,
  input  A,
  input  B,
  input  [2:0] ALU_Opt,
  input  Ainv,
  input  Binv,
  input  SLT,
  output Result,
  output Cout,
  output Sign
);

  wire A_neg, Aop, B_neg, Bop, overflow_1_r, r_and, r_or, r_sum;
  wire [1:0] decoder_alu_1_out_4;

  not not_1 (A_neg, A);
  not not_2 (B_neg, B);
  Multiplexer #(.enable("false")) multiplexer_1 (.in0(A), .in1(A_neg), .out(Aop), .sel(Ainv));
  Multiplexer #(.enable("false")) multiplexer_2 (.in0(B), .in1(B_neg), .out(Bop), .sel(Binv));
  OverFlow overflow_1 (.A(Cin), .B(Cout), .R(overflow_1_r));
  or or_1 (r_or, Aop, Bop);
  and and_1 (r_and, Aop, Bop);
  FA_1bit fa_1bit_1 (.A(Aop), .B(Bop), .Cin(Cin), .Sum(r_sum), .Cout(Cout));
  SignCalculator signcalculator_1 (.A(r_sum), .B(Cout), .Overflow(overflow_1_r), .sgn(Sign));
  Multiplexer #(.select(2), .enable("false")) multiplexer_3 (
    .in0(r_and), .in1(r_or), .in2(r_sum), .in3(SLT), .out(Result), .sel(decoder_alu_1_out_4));
  Decoder_ALU decoder_alu_1 (.in_1(ALU_Opt[2]), .in_2(ALU_Opt[1]), .in_3(ALU_Opt[0]), .out_4(decoder_alu_1_out_4));

  // Other names for the same wires on the sheet: r_slt = SLT
endmodule

module FA_1bit (
  input  A,
  input  B,
  input  Cin,
  output Sum,
  output Cout
);

  wire and_1_out, and_2_out, and_3_out, and_4_out, and_5_out, and_6_out, and_7_out, not_1_out, not_2_out,
       not_3_out, not_4_out, not_5_out, not_6_out;

  not not_1 (not_1_out, A);
  not not_2 (not_2_out, B);
  not not_3 (not_3_out, A);
  not not_4 (not_4_out, Cin);
  not not_5 (not_5_out, B);
  not not_6 (not_6_out, Cin);
  and and_1 (and_1_out, B, Cin);
  and and_2 (and_2_out, A, Cin);
  and and_3 (and_3_out, A, B);
  and and_4 (and_4_out, not_1_out, not_2_out, Cin);
  and and_5 (and_5_out, not_3_out, B, not_4_out);
  and and_6 (and_6_out, A, not_5_out, not_6_out);
  and and_7 (and_7_out, A, B, Cin);
  or or_1 (Cout, and_1_out, and_2_out, and_3_out);
  or or_2 (Sum, and_4_out, and_5_out, and_6_out, and_7_out);
endmodule

module OverFlow (
  input  A,
  input  B,
  output R
);

  wire and_1_out, and_2_out, not_1_out, not_2_out;

  not not_1 (not_1_out, B);
  not not_2 (not_2_out, A);
  and and_1 (and_1_out, A, not_1_out);
  and and_2 (and_2_out, B, not_2_out);
  or or_1 (R, and_1_out, and_2_out);
endmodule

module SignCalculator (
  input  A,
  input  B,
  input  Overflow,
  output sgn
);

  Multiplexer #(.enable("false")) multiplexer_1 (.in0(A), .in1(B), .out(sgn), .sel(Overflow));
endmodule

module ALU_32bit (
  input  [2:0] ALU_Op,
  input  [31:0] b,
  input  [31:0] a,
  output [31:0] R,
  output Zero
);

  wire Ainv, alu_1bit_1_cout, alu_1bit_2_cout, alu_1bit_3_cout, alu_1bit_4_cout, alu_1bit_5_cout,
       alu_1bit_6_cout, alu_1bit_7_cout, alu_1bit_8_cout, alu_1bit_9_cout, alu_1bit_10_cout,
       alu_1bit_11_cout, alu_1bit_12_cout, alu_1bit_13_cout, alu_1bit_14_cout, alu_1bit_15_cout,
       alu_1bit_16_cout, alu_1bit_17_cout, alu_1bit_18_cout, alu_1bit_19_cout, alu_1bit_20_cout,
       alu_1bit_21_cout, alu_1bit_22_cout, alu_1bit_23_cout, alu_1bit_24_cout, alu_1bit_25_cout,
       alu_1bit_26_cout, alu_1bit_27_cout, alu_1bit_28_cout, alu_1bit_29_cout, alu_1bit_30_cout,
       alu_1bit_31_cout, Binv, or_1_out, Sign;

  or or_1 (or_1_out, R[0], R[1], R[2], R[3], R[4], R[5], R[6], R[7], R[8], R[9], R[10], R[11], R[12], R[13], R[14], R[15], R[16], R[17], R[18], R[19], R[20], R[21], R[22], R[23], R[24], R[25], R[26], R[27], R[28], R[29], R[30], R[31]);
  not not_1 (Zero, or_1_out);
  Set_Ainv set_ainv_1 (.in_1(ALU_Op), .out_2(Ainv));
  Set_Binv set_binv_1 (.in_1(ALU_Op), .out_2(Binv));
  ALU_1bit alu_1bit_1 (
    .Cin(Binv), .A(a[0]), .B(b[0]), .ALU_Opt(ALU_Op), .Ainv(Ainv), .Binv(Binv), .SLT(Sign), .Result(R[0]),
    .Cout(alu_1bit_1_cout));  // open: Sign
  ALU_1bit alu_1bit_2 (
    .Cin(alu_1bit_1_cout), .A(a[1]), .B(b[1]), .ALU_Opt(ALU_Op), .Ainv(Ainv), .Binv(Binv), .SLT(1'b0),
    .Result(R[1]), .Cout(alu_1bit_2_cout));  // open: Sign
  ALU_1bit alu_1bit_3 (
    .Cin(alu_1bit_2_cout), .A(a[2]), .B(b[2]), .ALU_Opt(ALU_Op), .Ainv(Ainv), .Binv(Binv), .SLT(1'b0),
    .Result(R[2]), .Cout(alu_1bit_3_cout));  // open: Sign
  ALU_1bit alu_1bit_4 (
    .Cin(alu_1bit_3_cout), .A(a[3]), .B(b[3]), .ALU_Opt(ALU_Op), .Ainv(Ainv), .Binv(Binv), .SLT(1'b0),
    .Result(R[3]), .Cout(alu_1bit_4_cout));  // open: Sign
  ALU_1bit alu_1bit_5 (
    .Cin(alu_1bit_4_cout), .A(a[4]), .B(b[4]), .ALU_Opt(ALU_Op), .Ainv(Ainv), .Binv(Binv), .SLT(1'b0),
    .Result(R[4]), .Cout(alu_1bit_5_cout));  // open: Sign
  ALU_1bit alu_1bit_6 (
    .Cin(alu_1bit_5_cout), .A(a[5]), .B(b[5]), .ALU_Opt(ALU_Op), .Ainv(Ainv), .Binv(Binv), .SLT(1'b0),
    .Result(R[5]), .Cout(alu_1bit_6_cout));  // open: Sign
  ALU_1bit alu_1bit_7 (
    .Cin(alu_1bit_6_cout), .A(a[6]), .B(b[6]), .ALU_Opt(ALU_Op), .Ainv(Ainv), .Binv(Binv), .SLT(1'b0),
    .Result(R[6]), .Cout(alu_1bit_7_cout));  // open: Sign
  ALU_1bit alu_1bit_8 (
    .Cin(alu_1bit_7_cout), .A(a[7]), .B(b[7]), .ALU_Opt(ALU_Op), .Ainv(Ainv), .Binv(Binv), .SLT(1'b0),
    .Result(R[7]), .Cout(alu_1bit_8_cout));  // open: Sign
  ALU_1bit alu_1bit_9 (
    .Cin(alu_1bit_8_cout), .A(a[8]), .B(b[8]), .ALU_Opt(ALU_Op), .Ainv(Ainv), .Binv(Binv), .SLT(1'b0),
    .Result(R[8]), .Cout(alu_1bit_9_cout));  // open: Sign
  ALU_1bit alu_1bit_10 (
    .Cin(alu_1bit_9_cout), .A(a[9]), .B(b[9]), .ALU_Opt(ALU_Op), .Ainv(Ainv), .Binv(Binv), .SLT(1'b0),
    .Result(R[9]), .Cout(alu_1bit_10_cout));  // open: Sign
  ALU_1bit alu_1bit_11 (
    .Cin(alu_1bit_10_cout), .A(a[10]), .B(b[10]), .ALU_Opt(ALU_Op), .Ainv(Ainv), .Binv(Binv), .SLT(1'b0),
    .Result(R[10]), .Cout(alu_1bit_11_cout));  // open: Sign
  ALU_1bit alu_1bit_12 (
    .Cin(alu_1bit_11_cout), .A(a[11]), .B(b[11]), .ALU_Opt(ALU_Op), .Ainv(Ainv), .Binv(Binv), .SLT(1'b0),
    .Result(R[11]), .Cout(alu_1bit_12_cout));  // open: Sign
  ALU_1bit alu_1bit_13 (
    .Cin(alu_1bit_12_cout), .A(a[12]), .B(b[12]), .ALU_Opt(ALU_Op), .Ainv(Ainv), .Binv(Binv), .SLT(1'b0),
    .Result(R[12]), .Cout(alu_1bit_13_cout));  // open: Sign
  ALU_1bit alu_1bit_14 (
    .Cin(alu_1bit_13_cout), .A(a[13]), .B(b[13]), .ALU_Opt(ALU_Op), .Ainv(Ainv), .Binv(Binv), .SLT(1'b0),
    .Result(R[13]), .Cout(alu_1bit_14_cout));  // open: Sign
  ALU_1bit alu_1bit_15 (
    .Cin(alu_1bit_14_cout), .A(a[14]), .B(b[14]), .ALU_Opt(ALU_Op), .Ainv(Ainv), .Binv(Binv), .SLT(1'b0),
    .Result(R[14]), .Cout(alu_1bit_15_cout));  // open: Sign
  ALU_1bit alu_1bit_16 (
    .Cin(alu_1bit_15_cout), .A(a[15]), .B(b[15]), .ALU_Opt(ALU_Op), .Ainv(Ainv), .Binv(Binv), .SLT(1'b0),
    .Result(R[15]), .Cout(alu_1bit_16_cout));  // open: Sign
  ALU_1bit alu_1bit_17 (
    .Cin(alu_1bit_16_cout), .A(a[16]), .B(b[16]), .ALU_Opt(ALU_Op), .Ainv(Ainv), .Binv(Binv), .SLT(1'b0),
    .Result(R[16]), .Cout(alu_1bit_17_cout));  // open: Sign
  ALU_1bit alu_1bit_18 (
    .Cin(alu_1bit_17_cout), .A(a[17]), .B(b[17]), .ALU_Opt(ALU_Op), .Ainv(Ainv), .Binv(Binv), .SLT(1'b0),
    .Result(R[17]), .Cout(alu_1bit_18_cout));  // open: Sign
  ALU_1bit alu_1bit_19 (
    .Cin(alu_1bit_18_cout), .A(a[18]), .B(b[18]), .ALU_Opt(ALU_Op), .Ainv(Ainv), .Binv(Binv), .SLT(1'b0),
    .Result(R[18]), .Cout(alu_1bit_19_cout));  // open: Sign
  ALU_1bit alu_1bit_20 (
    .Cin(alu_1bit_19_cout), .A(a[19]), .B(b[19]), .ALU_Opt(ALU_Op), .Ainv(Ainv), .Binv(Binv), .SLT(1'b0),
    .Result(R[19]), .Cout(alu_1bit_20_cout));  // open: Sign
  ALU_1bit alu_1bit_21 (
    .Cin(alu_1bit_20_cout), .A(a[20]), .B(b[20]), .ALU_Opt(ALU_Op), .Ainv(Ainv), .Binv(Binv), .SLT(1'b0),
    .Result(R[20]), .Cout(alu_1bit_21_cout));  // open: Sign
  ALU_1bit alu_1bit_22 (
    .Cin(alu_1bit_21_cout), .A(a[21]), .B(b[21]), .ALU_Opt(ALU_Op), .Ainv(Ainv), .Binv(Binv), .SLT(1'b0),
    .Result(R[21]), .Cout(alu_1bit_22_cout));  // open: Sign
  ALU_1bit alu_1bit_23 (
    .Cin(alu_1bit_22_cout), .A(a[22]), .B(b[22]), .ALU_Opt(ALU_Op), .Ainv(Ainv), .Binv(Binv), .SLT(1'b0),
    .Result(R[22]), .Cout(alu_1bit_23_cout));  // open: Sign
  ALU_1bit alu_1bit_24 (
    .Cin(alu_1bit_23_cout), .A(a[23]), .B(b[23]), .ALU_Opt(ALU_Op), .Ainv(Ainv), .Binv(Binv), .SLT(1'b0),
    .Result(R[23]), .Cout(alu_1bit_24_cout));  // open: Sign
  ALU_1bit alu_1bit_25 (
    .Cin(alu_1bit_24_cout), .A(a[24]), .B(b[24]), .ALU_Opt(ALU_Op), .Ainv(Ainv), .Binv(Binv), .SLT(1'b0),
    .Result(R[24]), .Cout(alu_1bit_25_cout));  // open: Sign
  ALU_1bit alu_1bit_26 (
    .Cin(alu_1bit_25_cout), .A(a[25]), .B(b[25]), .ALU_Opt(ALU_Op), .Ainv(Ainv), .Binv(Binv), .SLT(1'b0),
    .Result(R[25]), .Cout(alu_1bit_26_cout));  // open: Sign
  ALU_1bit alu_1bit_27 (
    .Cin(alu_1bit_26_cout), .A(a[26]), .B(b[26]), .ALU_Opt(ALU_Op), .Ainv(Ainv), .Binv(Binv), .SLT(1'b0),
    .Result(R[26]), .Cout(alu_1bit_27_cout));  // open: Sign
  ALU_1bit alu_1bit_28 (
    .Cin(alu_1bit_27_cout), .A(a[27]), .B(b[27]), .ALU_Opt(ALU_Op), .Ainv(Ainv), .Binv(Binv), .SLT(1'b0),
    .Result(R[27]), .Cout(alu_1bit_28_cout));  // open: Sign
  ALU_1bit alu_1bit_29 (
    .Cin(alu_1bit_28_cout), .A(a[28]), .B(b[28]), .ALU_Opt(ALU_Op), .Ainv(Ainv), .Binv(Binv), .SLT(1'b0),
    .Result(R[28]), .Cout(alu_1bit_29_cout));  // open: Sign
  ALU_1bit alu_1bit_30 (
    .Cin(alu_1bit_29_cout), .A(a[29]), .B(b[29]), .ALU_Opt(ALU_Op), .Ainv(Ainv), .Binv(Binv), .SLT(1'b0),
    .Result(R[29]), .Cout(alu_1bit_30_cout));  // open: Sign
  ALU_1bit alu_1bit_31 (
    .Cin(alu_1bit_30_cout), .A(a[30]), .B(b[30]), .ALU_Opt(ALU_Op), .Ainv(Ainv), .Binv(Binv), .SLT(1'b0),
    .Result(R[30]), .Cout(alu_1bit_31_cout));  // open: Sign
  ALU_1bit alu_1bit_32 (
    .Cin(alu_1bit_31_cout), .A(a[31]), .B(b[31]), .ALU_Opt(ALU_Op), .Ainv(Ainv), .Binv(Binv), .SLT(1'b0),
    .Result(R[31]), .Sign(Sign));  // open: Cout
endmodule

module Decoder_ALU (
  input  in_1,
  input  in_2,
  input  in_3,
  output [1:0] out_4
);

  wire and_1_out, and_2_out, BNEG;

  and and_1 (and_1_out, in_1, in_3);
  not not_1 (BNEG, in_2);
  and and_2 (and_2_out, in_1, BNEG);
  or or_1 (out_4[0], and_2_out, and_1_out);

  assign out_4[1] = in_2;

  // Other names for the same wires on the sheet: A = in_1; C = in_3; B = in_2
endmodule

module ALU_4bits (
  input  [3:0] a,
  input  [3:0] b,
  input  [2:0] Alu_Op,
  output [3:0] R
);

  wire Ainv, alu_1bit_1_cout, alu_1bit_2_cout, alu_1bit_3_cout, Binv, Sign;

  Set_Ainv set_ainv_1 (.in_1(Alu_Op), .out_2(Ainv));
  Set_Binv set_binv_1 (.in_1(Alu_Op), .out_2(Binv));
  ALU_1bit alu_1bit_1 (
    .Cin(Binv), .A(a[0]), .B(b[0]), .ALU_Opt(Alu_Op), .Ainv(Ainv), .Binv(Binv), .SLT(Sign), .Result(R[0]),
    .Cout(alu_1bit_1_cout));  // open: Sign
  ALU_1bit alu_1bit_2 (
    .Cin(alu_1bit_1_cout), .A(a[1]), .B(b[1]), .ALU_Opt(Alu_Op), .Ainv(Ainv), .Binv(Binv), .SLT(1'b0),
    .Result(R[1]), .Cout(alu_1bit_2_cout));  // open: Sign
  ALU_1bit alu_1bit_3 (
    .Cin(alu_1bit_2_cout), .A(a[2]), .B(b[2]), .ALU_Opt(Alu_Op), .Ainv(Ainv), .Binv(Binv), .SLT(1'b0),
    .Result(R[2]), .Cout(alu_1bit_3_cout));  // open: Sign
  ALU_1bit alu_1bit_4 (
    .Cin(alu_1bit_3_cout), .A(a[3]), .B(b[3]), .ALU_Opt(Alu_Op), .Ainv(Ainv), .Binv(Binv), .SLT(1'b0),
    .Result(R[3]), .Sign(Sign));  // open: Cout
endmodule

module Set_Ainv (
  input  [2:0] in_1,
  output out_2
);

  wire not_1_out;

  not not_1 (not_1_out, in_1[1]);
  and and_1 (out_2, in_1[0], not_1_out);
endmodule

module Set_Binv (
  input  [2:0] in_1,
  output out_2
);

  wire and_1_out, and_2_out, not_1_out;

  not not_1 (not_1_out, in_1[1]);
  and and_1 (and_1_out, in_1[2], in_1[1]);
  and and_2 (and_2_out, not_1_out, in_1[0]);
  or or_1 (out_2, and_1_out, and_2_out);
endmodule

module ALU_Control (
  input  Op1,
  input  Op0,
  input  Func5,
  input  Func4,
  input  Func3,
  input  Func2,
  input  Func1,
  input  Func0,
  output [2:0] out_9
);

  wire and_1_out, and_2_out, and_3_out, and_4_out, and_5_out, and_6_out, and_7_out, and_8_out, and_9_out,
       and_10_out, and_11_out, and_12_out, and_13_out, and_14_out, and_15_out, Aneg, Bneg, Cneg, Dneg, Eneg,
       Fneg, Gneg, Hneg, or_1_out, or_2_out, or_5_out;

  not not_1 (Aneg, Op1);
  not not_2 (Bneg, Op0);
  not not_3 (Cneg, Func5);
  not not_4 (Dneg, Func4);
  not not_5 (Eneg, Func3);
  not not_6 (Fneg, Func2);
  not not_7 (Gneg, Func1);
  not not_8 (Hneg, Func0);
  and and_1 (and_1_out, Eneg, Func2, Gneg, Func0);
  and and_2 (and_2_out, Fneg, Func1, Hneg);
  and and_3 (and_3_out, Eneg, Func2, Func1, Func0);
  and and_4 (and_4_out, Eneg, Fneg, Gneg, Hneg);
  and and_5 (and_5_out, Func3, Fneg, Func1, Hneg);
  and and_6 (and_6_out, Op1, Bneg, Func5, Dneg);
  or or_1 (or_1_out, and_1_out, and_2_out);
  and and_7 (and_7_out, Op1, Bneg, Func5, Dneg);
  or or_2 (or_2_out, and_4_out, and_3_out, and_5_out);
  and and_8 (and_8_out, Aneg, Op0);
  and and_9 (and_9_out, and_6_out, or_1_out);
  and and_10 (and_10_out, Aneg, Bneg);
  and and_11 (and_11_out, and_7_out, or_2_out);
  or or_3 (out_9[2], and_8_out, and_9_out);
  or or_4 (out_9[0], and_10_out, and_11_out);
  and and_12 (and_12_out, Eneg, Fneg, Hneg);
  and and_13 (and_13_out, Fneg, Func1, Hneg);
  and and_14 (and_14_out, Op1, Bneg, Func5, Dneg);
  or or_5 (or_5_out, and_12_out, and_13_out);
  and and_15 (and_15_out, and_14_out, or_5_out);
  or or_6 (out_9[1], Aneg, and_15_out);

  // Other names for the same wires on the sheet: A = Op1; B = Op0; C = Func5; D = Func4; E = Func3; F = Func2;
  //   G = Func1; H = Func0; Z = out_9[0]; Y = out_9[1]; X = out_9[2]
endmodule

module MAIN_CONTROL (
  input  Op5,
  input  Op4,
  input  Op3,
  input  Op2,
  input  Op1,
  input  Op0,
  output Regdst,
  output ALUSrc,
  output MemtoReg,
  output RegWrite,
  output MemRead,
  output MemWrite,
  output Branch,
  output ALUOp1,
  output ALUOp0
);

  wire Aneg, Bneg, Cneg, Dneg, Eneg, Fneg;

  not not_1 (Aneg, Op5);
  not not_2 (Bneg, Op4);
  not not_3 (Cneg, Op3);
  not not_4 (Dneg, Op2);
  not not_5 (Eneg, Op1);
  not not_6 (Fneg, Op0);
  and and_1 (Regdst, Aneg, Bneg, Cneg, Dneg, Eneg, Fneg);
  and and_2 (ALUSrc, Op5, Bneg, Dneg, Op1, Op0);
  and and_3 (MemtoReg, Op5, Bneg, Cneg, Dneg, Op1, Op0);
  and and_4 (RegWrite, Cneg, Dneg);
  and and_5 (MemRead, Op5, Bneg, Cneg, Dneg, Op1, Op0);
  and and_6 (MemWrite, Op5, Bneg, Op3, Dneg, Op1, Op0);
  and and_7 (Branch, Aneg, Bneg, Cneg, Op2, Eneg, Fneg);
  and and_8 (ALUOp1, Aneg, Bneg, Cneg, Dneg, Eneg, Fneg);
  and and_9 (ALUOp0, Aneg, Bneg, Cneg, Op2, Eneg, Fneg);

  // Other names for the same wires on the sheet: A = Op5; B = Op4; C = Op3; D = Op2; E = Op1; F = Op0
endmodule

module Reg_File (
  input  CLK,
  input  Reset,
  input  [31:0] Write_Data,
  input  [4:0] Read_Reg_1,
  input  [4:0] Read_Reg_2,
  input  Reg_Write,
  input  [4:0] Write_Reg,
  output [31:0] out_8,
  output [31:0] out_9
);

  wire decoder_1_out0, decoder_1_out1, decoder_1_out2, decoder_1_out3, decoder_1_out4, decoder_1_out5,
       decoder_1_out6, decoder_1_out7, decoder_1_out8, decoder_1_out9, decoder_1_out10, decoder_1_out11,
       decoder_1_out12, decoder_1_out13, decoder_1_out14, decoder_1_out15, decoder_1_out16, decoder_1_out17,
       decoder_1_out18, decoder_1_out19, decoder_1_out20, decoder_1_out21, decoder_1_out22, decoder_1_out23,
       decoder_1_out24, decoder_1_out25, decoder_1_out26, decoder_1_out27, decoder_1_out28, decoder_1_out29,
       decoder_1_out30, decoder_1_out31;
  wire [31:0] R0, R1, R2, R3, R4, R5, R6, R7, R8, R9, R10, R11, R12, R13, R14, R15, R16, R17, R18, R19, R20,
       R21, R22, R23, R24, R25, R26, R27, R28, R29, R30, R31;

  Decoder #(.select(5)) decoder_1 (
    .out0(decoder_1_out0), .out1(decoder_1_out1), .out2(decoder_1_out2), .out3(decoder_1_out3),
    .out4(decoder_1_out4), .out5(decoder_1_out5), .out6(decoder_1_out6), .out7(decoder_1_out7),
    .out8(decoder_1_out8), .out9(decoder_1_out9), .out10(decoder_1_out10), .out11(decoder_1_out11),
    .out12(decoder_1_out12), .out13(decoder_1_out13), .out14(decoder_1_out14), .out15(decoder_1_out15),
    .out16(decoder_1_out16), .out17(decoder_1_out17), .out18(decoder_1_out18), .out19(decoder_1_out19),
    .out20(decoder_1_out20), .out21(decoder_1_out21), .out22(decoder_1_out22), .out23(decoder_1_out23),
    .out24(decoder_1_out24), .out25(decoder_1_out25), .out26(decoder_1_out26), .out27(decoder_1_out27),
    .out28(decoder_1_out28), .out29(decoder_1_out29), .out30(decoder_1_out30), .out31(decoder_1_out31),
    .sel(Write_Reg), .en(Reg_Write));
  Register #(.width(32)) register_1 (.D(Write_Data), .en(decoder_1_out0), .clk(CLK), .Q(R0), .clr(Reset));
  Register #(.width(32)) register_2 (.D(Write_Data), .en(decoder_1_out1), .clk(CLK), .Q(R1), .clr(Reset));
  Register #(.width(32)) register_3 (.D(Write_Data), .en(decoder_1_out2), .clk(CLK), .Q(R2), .clr(Reset));
  Register #(.width(32)) register_4 (.D(Write_Data), .en(decoder_1_out3), .clk(CLK), .Q(R3), .clr(Reset));
  Register #(.width(32)) register_5 (.D(Write_Data), .en(decoder_1_out4), .clk(CLK), .Q(R4), .clr(Reset));
  Register #(.width(32)) register_6 (.D(Write_Data), .en(decoder_1_out5), .clk(CLK), .Q(R5), .clr(Reset));
  Register #(.width(32)) register_7 (.D(Write_Data), .en(decoder_1_out6), .clk(CLK), .Q(R6), .clr(Reset));
  Register #(.width(32)) register_8 (.D(Write_Data), .en(decoder_1_out7), .clk(CLK), .Q(R7), .clr(Reset));
  Register #(.width(32)) register_9 (.D(Write_Data), .en(decoder_1_out8), .clk(CLK), .Q(R8), .clr(Reset));
  Register #(.width(32)) register_10 (.D(Write_Data), .en(decoder_1_out9), .clk(CLK), .Q(R9), .clr(Reset));
  Register #(.width(32)) register_11 (.D(Write_Data), .en(decoder_1_out10), .clk(CLK), .Q(R10), .clr(Reset));
  Register #(.width(32)) register_12 (.D(Write_Data), .en(decoder_1_out11), .clk(CLK), .Q(R11), .clr(Reset));
  Register #(.width(32)) register_13 (.D(Write_Data), .en(decoder_1_out12), .clk(CLK), .Q(R12), .clr(Reset));
  Register #(.width(32)) register_14 (.D(Write_Data), .en(decoder_1_out13), .clk(CLK), .Q(R13), .clr(Reset));
  Register #(.width(32)) register_15 (.D(Write_Data), .en(decoder_1_out14), .clk(CLK), .Q(R14), .clr(Reset));
  Register #(.width(32)) register_16 (.D(Write_Data), .en(decoder_1_out15), .clk(CLK), .Q(R15), .clr(Reset));
  Register #(.width(32)) register_17 (.D(Write_Data), .en(decoder_1_out16), .clk(CLK), .Q(R16), .clr(Reset));
  Register #(.width(32)) register_18 (.D(Write_Data), .en(decoder_1_out17), .clk(CLK), .Q(R17), .clr(Reset));
  Register #(.width(32)) register_19 (.D(Write_Data), .en(decoder_1_out18), .clk(CLK), .Q(R18), .clr(Reset));
  Register #(.width(32)) register_20 (.D(Write_Data), .en(decoder_1_out19), .clk(CLK), .Q(R19), .clr(Reset));
  Register #(.width(32)) register_21 (.D(Write_Data), .en(decoder_1_out20), .clk(CLK), .Q(R20), .clr(Reset));
  Register #(.width(32)) register_22 (.D(Write_Data), .en(decoder_1_out21), .clk(CLK), .Q(R21), .clr(Reset));
  Register #(.width(32)) register_23 (.D(Write_Data), .en(decoder_1_out22), .clk(CLK), .Q(R22), .clr(Reset));
  Register #(.width(32)) register_24 (.D(Write_Data), .en(decoder_1_out23), .clk(CLK), .Q(R23), .clr(Reset));
  Register #(.width(32)) register_25 (.D(Write_Data), .en(decoder_1_out24), .clk(CLK), .Q(R24), .clr(Reset));
  Register #(.width(32)) register_26 (.D(Write_Data), .en(decoder_1_out25), .clk(CLK), .Q(R25), .clr(Reset));
  Register #(.width(32)) register_27 (.D(Write_Data), .en(decoder_1_out26), .clk(CLK), .Q(R26), .clr(Reset));
  Register #(.width(32)) register_28 (.D(Write_Data), .en(decoder_1_out27), .clk(CLK), .Q(R27), .clr(Reset));
  Register #(.width(32)) register_29 (.D(Write_Data), .en(decoder_1_out28), .clk(CLK), .Q(R28), .clr(Reset));
  Register #(.width(32)) register_30 (.D(Write_Data), .en(decoder_1_out29), .clk(CLK), .Q(R29), .clr(Reset));
  Register #(.width(32)) register_31 (.D(Write_Data), .en(decoder_1_out30), .clk(CLK), .Q(R30), .clr(Reset));
  Register #(.width(32)) register_32 (.D(Write_Data), .en(decoder_1_out31), .clk(CLK), .Q(R31), .clr(Reset));
  Multiplexer #(.select(5), .width(32), .enable("false")) multiplexer_1 (
    .in0(R0), .in1(R1), .in2(R2), .in3(R3), .in4(R4), .in5(R5), .in6(R6), .in7(R7), .in8(R8), .in9(R9),
    .in10(R10), .in11(R11), .in12(R12), .in13(R13), .in14(R14), .in15(R15), .in16(R16), .in17(R17),
    .in18(R18), .in19(R19), .in20(R20), .in21(R21), .in22(R22), .in23(R23), .in24(R24), .in25(R25),
    .in26(R26), .in27(R27), .in28(R28), .in29(R29), .in30(R30), .in31(R31), .out(out_8), .sel(Read_Reg_1));
  Multiplexer #(.select(5), .width(32), .enable("false")) multiplexer_2 (
    .in0(R0), .in1(R1), .in2(R2), .in3(R3), .in4(R4), .in5(R5), .in6(R6), .in7(R7), .in8(R8), .in9(R9),
    .in10(R10), .in11(R11), .in12(R12), .in13(R13), .in14(R14), .in15(R15), .in16(R16), .in17(R17),
    .in18(R18), .in19(R19), .in20(R20), .in21(R21), .in22(R22), .in23(R23), .in24(R24), .in25(R25),
    .in26(R26), .in27(R27), .in28(R28), .in29(R29), .in30(R30), .in31(R31), .out(out_9), .sel(Read_Reg_2));

  // Other names for the same wires on the sheet: RR1[4:0] = Read_Reg_1; RR2[4:0] = Read_Reg_2
endmodule
