// Logisim project lab4.circ as structural Verilog
module ALU_1bit (
  input  Cin,
  input  A,
  input  B,
  input  Ainv,
  input  [2:0] ALU_Opt,
  input  Binv,
  input  SLT,
  output Result,
  output Cout,
  output Sign
);

  wire A_neg, Aop, B_neg, Bop, overflow_1_r, r_and, r_or;

  not not_1 (A_neg, A);
  not not_2 (B_neg, B);
  Multiplexer #(.enable("false")) multiplexer_1 (.in0(A), .in1(A_neg), .out(Aop), .sel(Ainv));
  Multiplexer #(.enable("false")) multiplexer_2 (.in0(B), .in1(B_neg), .out(Bop), .sel(Binv));
  or or_1 (r_or, Aop, Bop);
  and and_1 (r_and, Aop, Bop);
  FA_1bit fa_1bit_1 (.A(Aop), .B(Bop), .Cin(Cin), .Sum(Sign), .Cout(Cout));
  OverFlow overflow_1 (.A(Cin), .B(Cout), .R(overflow_1_r));
  SignCalculator signcalculator_1 (.A(Sign), .B(Cout), .Overflow(overflow_1_r), .sgn(SLT));
  Multiplexer #(.select(3), .enable("false")) multiplexer_3 (
    .in0(r_and), .in3(Sign), .in4(r_or), .in7(SLT), .out(Result), .sel(ALU_Opt));  // open: in1, in2, in5, in6

  // Other names for the same wires on the sheet: r_slt = SLT; r_sum = Sign
endmodule

module FA_1bit (
  input  A,
  input  B,
  input  Cin,
  output Sum,
  output Cout
);

  wire and_1_out, and_2_out, and_3_out, and_4_out, and_5_out, and_6_out, and_7_out, not_1_out, not_2_out,
       not_3_out, not_4_out, not_5_out, not_6_out;

  not not_1 (not_1_out, A);
  not not_2 (not_2_out, B);
  not not_3 (not_3_out, A);
  not not_4 (not_4_out, Cin);
  not not_5 (not_5_out, B);
  not not_6 (not_6_out, Cin);
  and and_1 (and_1_out, B, Cin);
  and and_2 (and_2_out, A, Cin);
  and and_3 (and_3_out, A, B);
  and and_4 (and_4_out, not_1_out, not_2_out, Cin);
  and and_5 (and_5_out, not_3_out, B, not_4_out);
  and and_6 (and_6_out, A, not_5_out, not_6_out);
  and and_7 (and_7_out, A, B, Cin);
  or or_1 (Cout, and_1_out, and_2_out, and_3_out);
  or or_2 (Sum, and_4_out, and_5_out, and_6_out, and_7_out);
endmodule

module OverFlow (
  input  A,
  input  B,
  output R
);

  wire and_1_out, and_2_out, not_1_out, not_2_out;

  not not_1 (not_1_out, B);
  not not_2 (not_2_out, A);
  and and_1 (and_1_out, A, not_1_out);
  and and_2 (and_2_out, B, not_2_out);
  or or_1 (R, and_1_out, and_2_out);
endmodule

module SignCalculator (
  input  A,
  input  B,
  input  Overflow,
  output sgn
);

  Multiplexer #(.enable("false")) multiplexer_1 (.in0(B), .in1(A), .out(sgn), .sel(Overflow));
endmodule

module ALU_32bit (
  input  [3:0] ALU_Operation,
  input  [31:0] a,
  input  [31:0] b,
  output out_4,
  output [31:0] R
);


  assign out_4 = 1'b0;

  // Other names for the same wires on the sheet: b0 = a[0]; b1 = a[1]; b2 = a[2]; b3 = a[3]; b4 = a[4]; b5 = a[5];
  //   b6 = a[6]; b7 = a[7]; b8 = a[8]; b9 = a[9]; b10 = a[10]; b11 = a[11]; b12 = a[12]; b13 = a[13]; b14 = a[14];
  //   b15 = a[15]; b16 = a[16]; b17 = a[17]; b18 = a[18]; b19 = a[19]; b20 = a[20]; b21 = a[21]; b22 = a[22];
  //   b23 = a[23]; b24 = a[24]; b25 = a[25]; b26 = a[26]; b27 = a[27]; b28 = a[28]; b29 = a[29]; b30 = a[30];
  //   b31 = a[31]; ALU_Opt0 = ALU_Operation[0]; ALU_Opt1 = ALU_Operation[1]; binv = ALU_Operation[2];
  //   ainv = ALU_Operation[3]; a0 = b[0]; a1 = b[1]; a2 = b[2]; a3 = b[3]; a4 = b[4]; a5 = b[5]; a6 = b[6]; a7 = b[7];
  //   a8 = b[8]; a9 = b[9]; a10 = b[10]; a11 = b[11]; a12 = b[12]; a13 = b[13]; a14 = b[14]; a15 = b[15]; a16 = b[16];
  //   a17 = b[17]; a18 = b[18]; a19 = b[19]; a20 = b[20]; a21 = b[21]; a22 = b[22]; a23 = b[23]; a24 = b[24];
  //   a25 = b[25]; a26 = b[26]; a27 = b[27]; a28 = b[28]; a29 = b[29]; a30 = b[30]; a31 = b[31]

  // Notes on the sheet:
  //   0000     AND
  //   0001     OR
  //   0010     Add
  //   0110     Subtract
  //   1100     NOR
  //   0111     Set on les than
  //   Codificación para las operaciones de la ALU
  //   ALU_Operation (ainv, binv, ALU_Opt1, ALU_Opt0)
endmodule
